// Logisim project Experiment_10.circ as structural Verilog: 1 circuit, main circuit 4 bit ALU
module _4_bit_ALU (
  input  [3:0] A,
  input  [3:0] B,
  input  [1:0] OPCODE,
  output [3:0] OUTPUT
);

  wire [3:0] adder_1_out, divider_1_out, multiplier_1_out, subtractor_1_out;

  Adder #(.width(4)) adder_1 (.a(A), .b(B), .out(adder_1_out));  // open: cin, cout
  Subtractor #(.width(4)) subtractor_1 (.a(A), .b(B), .out(subtractor_1_out));  // open: bin, bout
  Multiplier #(.width(4)) multiplier_1 (.a(A), .b(B), .out(multiplier_1_out));  // open: cin, cout
  Divider #(.width(4)) divider_1 (.a(A), .b(B), .out(divider_1_out));  // open: upper, rem
  Multiplexer #(.select(2), .width(4), .enable("false")) multiplexer_1 (
    .in0(adder_1_out), .in1(subtractor_1_out), .in2(multiplier_1_out), .in3(divider_1_out), .out(OUTPUT),
    .sel(OPCODE));

  // Notes on the sheet:
  //   4 bit ALU Unit_PRIYANSHU_2100321540124
endmodule
