// Logisim project Experiment_11.circ as structural Verilog: 2 circuits, main circuit Half Subtractor
module Half_Subtractor (
  input  A,
  input  B,
  output Difference,
  output Borrow
);

  wire not_1_out;

  not not_1 (not_1_out, A);
  xor XOR (Difference, A, B);
  and AND (Borrow, not_1_out, B);

  // Notes on the sheet:
  //   Half Subtractor_PRIYANSHU_2100321540124
endmodule

module Full_Subtractor (
  input  A,
  input  B,
  input  Bin,
  output D,
  output Bout
);

  wire AND_2_out, AND_out, not_1_out, not_2_out, XOR_out;

  not not_1 (not_1_out, B);
  xor XOR (XOR_out, B, Bin);
  and AND (AND_out, not_1_out, Bin);
  xor XOR_2 (D, A, XOR_out);
  not not_2 (not_2_out, XOR_out);
  and AND_2 (AND_2_out, not_2_out, A);
  or OR (Bout, AND_2_out, AND_out);

  // Notes on the sheet:
  //   Full Subtractor_PRIYANSHU_2100321540124
endmodule
