// Logisim project Experiment_12.circ as structural Verilog: 1 circuit, main circuit Binary to BCD
module Binary_to_BCD (
  input  A,
  input  B,
  input  C,
  input  D,
  output W,
  output X,
  output Y,
  output Z,
  output E
);

  wire AND_2_out, AND_4_out, AND_5_out, AND_6_out, AND_7_out, AND_out, not_1_out, not_2_out, not_3_out;

  not not_1 (not_1_out, A);
  not not_2 (not_2_out, B);
  not not_3 (not_3_out, C);
  and AND (AND_out, A, B);
  or OR (W, AND_out, AND_2_out);
  and AND_2 (AND_2_out, A, C);
  and AND_3 (X, A, not_2_out, not_3_out);
  and AND_4 (AND_4_out, not_1_out, B);
  or OR_2 (Y, AND_4_out, AND_5_out);
  and AND_5 (AND_5_out, B, C);
  and AND_6 (AND_6_out, A, B, not_3_out);
  or OR_3 (Z, AND_6_out, AND_7_out);
  and AND_7 (AND_7_out, not_1_out, C);

  assign E = D;

  // Notes on the sheet:
  //   Binary to BCD_PRIYANSHU_2100321540124
endmodule
