// Logisim project Basic Circuits.circ as structural Verilog: 7 circuits, main circuit main
module main (
  input  INPUT_A,
  input  INPUT_B,
  output OUTPUT_Y
);

  and AND (OUTPUT_Y, INPUT_A, INPUT_B);

  // Notes on the sheet:
  //   AND GATE_PRIYANSHU_2100321540124
endmodule

module NAND (
  input  INPUT_A,
  input  INPUT_B,
  output OUTPUT
);

  wire AND_out;

  and AND (AND_out, INPUT_A, INPUT_B);
  not NOT (OUTPUT, AND_out);

  // Notes on the sheet:
  //   NAND GATE_PRIYANSHU_2100321540124
endmodule

module OR (
  input  INPUT_A,
  input  INPUT_B,
  output OUTPUT
);

  or OR (OUTPUT, INPUT_A, INPUT_B);

  // Notes on the sheet:
  //   OR GATE_PRIYANSHU_2100321540124
endmodule

module NOR (
  input  INPUT_A,
  input  INPUT_B,
  output OUTPUT
);

  nor NOR (OUTPUT, INPUT_A, INPUT_B);

  // Notes on the sheet:
  //   NOR GATE_PRIYANSHU_2100321540124
endmodule

module XOR (
  input  INPUT_A,
  input  INPUT_B,
  output OUTPUT
);

  xor XOR (OUTPUT, INPUT_A, INPUT_B);

  // Notes on the sheet:
  //   XOR GATE_PRIYANSHU_2100321540124
endmodule

module X_NOR (
  input  INPUT_A,
  input  INPUT_B,
  output OUTPUT
);

  xnor X_NOR (OUTPUT, INPUT_A, INPUT_B);

  // Notes on the sheet:
  //   X-NOR GATE_PRIYANSHU_2100321540124
endmodule

module NOT (
  input  INPUT,
  output OUTPUT
);

  not NOT (OUTPUT, INPUT);

  // Notes on the sheet:
  //   NOT GATE_PRIYANSHU_21003215401254
endmodule
