// Logisim project and.circ as structural Verilog: 1 circuit, main circuit main
module main (
  input  INPUT_A,
  input  INPUT_B,
  output OUTPUT_Y
);

  and AND (OUTPUT_Y, INPUT_A, INPUT_B);

  // Notes on the sheet:
  //   AND GATE_PRIYANSHU_2100321540124
endmodule
