// Logisim project GATES_USING_NAND.circ as structural Verilog
module and_using_nand (
  input  INPUT_A,
  input  INPUT_B,
  output OUTPUT_Y
);

  wire NAND_out;

  nand NAND (NAND_out, INPUT_A, INPUT_B);
  nand NAND_2 (OUTPUT_Y, NAND_out, NAND_out);

  // Notes on the sheet:
  //   AND GATE_PRIYANSHU_2100321540124
endmodule

module NOT_USING_NAND (
  input  INPUT_A,
  output OUTPUT_Y
);

  nand NAND (OUTPUT_Y, INPUT_A, INPUT_A);

  // Notes on the sheet:
  //   NOT GATE_PRIYANSHU_2100321540124
endmodule

module OR_USING_NAND (
  input  INPUT_A,
  input  INPUT_B,
  output OUTPUT_Y
);

  wire NAND_2_out, NAND_out;

  nand NAND (NAND_out, INPUT_A, INPUT_A);
  nand NAND_2 (NAND_2_out, INPUT_B, INPUT_B);
  nand NAND_3 (OUTPUT_Y, NAND_out, NAND_2_out);

  // Notes on the sheet:
  //   OR GATE_PRIYANSHU_2100321540124
endmodule

module XOR_USING_NAND (
  input  INPUT_A,
  input  INPUT_B,
  output OUTPUT_Y
);

  wire NAND_2_out, NAND_3_out, NAND_out;

  nand NAND (NAND_out, INPUT_A, INPUT_B);
  nand NAND_2 (NAND_2_out, INPUT_A, NAND_out);
  nand NAND_3 (NAND_3_out, NAND_out, INPUT_B);
  nand NAND_4 (OUTPUT_Y, NAND_2_out, NAND_3_out);

  // Notes on the sheet:
  //   XOR GATE_PRIYANSHU_2100321540124
endmodule

module NOR_USING_NAND (
  input  INPUT_A,
  input  INPUT_B,
  output OUTPUT_Y
);

  wire NAND_2_out, NAND_3_out, NAND_out;

  nand NAND (NAND_out, INPUT_A, INPUT_A);
  nand NAND_2 (NAND_2_out, INPUT_B, INPUT_B);
  nand NAND_3 (NAND_3_out, NAND_out, NAND_2_out);
  nand NAND_4 (OUTPUT_Y, NAND_3_out, NAND_3_out);

  // Notes on the sheet:
  //   NOR GATE_PRIYANSHU_2100321540124
endmodule

module XNOR_USING_NAND (
  input  INPUT_A,
  input  INPUT_B,
  output OUTPUT_Y
);

  wire NAND_2_out, NAND_3_out, NAND_4_out, NAND_out;

  nand NAND (NAND_out, INPUT_A, INPUT_B);
  nand NAND_2 (NAND_2_out, INPUT_A, NAND_out);
  nand NAND_3 (NAND_3_out, NAND_out, INPUT_B);
  nand NAND_4 (NAND_4_out, NAND_2_out, NAND_3_out);
  nand NAND_5 (OUTPUT_Y, NAND_4_out, NAND_4_out);

  // Notes on the sheet:
  //   XNOR GATE_PRIYANSHU_2100321540124
endmodule

module NAND_using_NOR (
  input  INPUT_A,
  input  INPUT_B,
  output OUTPUT_Y
);

  wire NOR_2_out, NOR_3_out, NOR_out;

  nor NOR (NOR_out, INPUT_A, INPUT_A);
  nor NOR_2 (NOR_2_out, INPUT_B, INPUT_B);
  nor NOR_3 (NOR_3_out, NOR_out, NOR_2_out);
  nor NOR_4 (OUTPUT_Y, NOR_3_out, NOR_3_out);

  // Notes on the sheet:
  //   NAND GATE_PRIYANSHU_2100321540124
endmodule
