// Logisim project GATES_USING_NOR.circ as structural Verilog
module NOT (
  input  INPUT_A,
  output OUTPUT_Y
);

  nor NOR (OUTPUT_Y, INPUT_A, INPUT_A);

  // Notes on the sheet:
  //   NOT GATE_PRIYANSHU_2100321540124
endmodule

module AND (
  input  INPUT_A,
  input  INPUT_B,
  output OUTPUT_Y
);

  wire NOR_2_out, NOR_out;

  nor NOR (NOR_out, INPUT_A, INPUT_A);
  nor NOR_2 (NOR_2_out, INPUT_B, INPUT_B);
  nor NOR_3 (OUTPUT_Y, NOR_out, NOR_2_out);

  // Notes on the sheet:
  //   AND GATE_PRIYANSHU_2100321540124
endmodule

module OR (
  input  INPUT_A,
  input  INPUT_B,
  output OUTPUT_Y
);

  wire NOR_out;

  nor NOR (NOR_out, INPUT_A, INPUT_B);
  nor NOR_2 (OUTPUT_Y, NOR_out, NOR_out);

  // Notes on the sheet:
  //   OR GATE_PRIYANSHU_2100321540124
endmodule

module XOR (
  input  INPUT_A,
  input  INPUT_B,
  output OUTPUT_Y
);

  wire NOR_2_out, NOR_3_out, NOR_4_out, NOR_out;

  nor NOR (NOR_out, INPUT_A, INPUT_B);
  nor NOR_2 (NOR_2_out, INPUT_A, NOR_out);
  nor NOR_3 (NOR_3_out, NOR_out, INPUT_B);
  nor NOR_4 (NOR_4_out, NOR_2_out, NOR_3_out);
  nor NOR_5 (OUTPUT_Y, NOR_4_out, NOR_4_out);

  // Notes on the sheet:
  //   XOR GATE_PRIYANSHU_2100321540124
endmodule

module XNOR (
  input  INPUT_A,
  input  INPUT_B,
  output OUTPUT_Y
);

  wire NOR_2_out, NOR_3_out, NOR_out;

  nor NOR (NOR_out, INPUT_A, INPUT_B);
  nor NOR_2 (NOR_2_out, INPUT_A, NOR_out);
  nor NOR_3 (NOR_3_out, NOR_out, INPUT_B);
  nor NOR_4 (OUTPUT_Y, NOR_2_out, NOR_3_out);

  // Notes on the sheet:
  //   XNOR GATE_PRIYANSHU_2100321540124
endmodule

module NAND (
  input  INPUT_A,
  input  INPUT_B,
  output OUTPUT_Y
);

  wire NOR_2_out, NOR_3_out, NOR_out;

  nor NOR (NOR_out, INPUT_A, INPUT_A);
  nor NOR_2 (NOR_2_out, INPUT_B, INPUT_B);
  nor NOR_3 (NOR_3_out, NOR_out, NOR_2_out);
  nor NOR_4 (OUTPUT_Y, NOR_3_out, NOR_3_out);

  // Notes on the sheet:
  //   NAND GATE_PRIYANSHU_2100321540124
endmodule
