// Logisim project ADDERS.circ as structural Verilog
module half_adder (
  input  INPUT_A,
  input  INPUT_B,
  output S,
  output C
);

  xor XOR (S, INPUT_A, INPUT_B);
  and AND (C, INPUT_A, INPUT_B);

  // Notes on the sheet:
  //   HALF ADDER_PRIYANSHU_2100321540124
endmodule

module FULL_ADDER (
  input  A,
  input  B,
  input  C_IN,
  output S,
  output C_OUT
);

  wire AND_2_out, AND_out, XOR_out;

  xor XOR (XOR_out, A, B);
  and AND (AND_out, A, B);
  xor XOR_2 (S, XOR_out, C_IN);
  and AND_2 (AND_2_out, XOR_out, C_IN);
  or OR (C_OUT, AND_out, AND_2_out);

  // Notes on the sheet:
  //   FULL ADDER_PRIYANSHU_2100321540124
endmodule
