// Logisim project conversion.circ as structural Verilog
module binary_to_grey (
  input  A,
  input  B,
  input  C,
  output G3,
  output G2,
  output G1
);

  xor XOR (G2, A, B);
  xor XOR_2 (G1, B, C);

  assign G3 = A;

  // Notes on the sheet:
  //   BINARY TO GREY_PRIYANSHU_2100321540124
endmodule

module GREY_TO_BINARY (
  input  A,
  input  B,
  input  C,
  output B3,
  output B2,
  output B1
);

  xor XOR (B2, A, B);
  xor XOR_2 (B1, B2, C);

  assign B3 = A;

  // Notes on the sheet:
  //   BINARY TO GREY_PRIYANSHU_2100321540124
endmodule
