// Logisim project Decoder.circ as structural Verilog
module _2_4_Decoder (
  input  E,
  input  A,
  input  B,
  output Output_0,
  output Output_1,
  output Output_2,
  output Output_3
);

  wire not_1_out, not_2_out;

  not not_1 (not_1_out, A);
  not not_2 (not_2_out, B);
  and AND (Output_0, not_1_out, not_2_out, E);
  and AND_2 (Output_1, B, not_1_out, E);
  and AND_3 (Output_2, not_2_out, A, E);
  and AND_4 (Output_3, B, A, E);
endmodule

module _3_8_Decoder (
  input  A2,
  input  A1,
  input  A0,
  output Output_0,
  output Output_1,
  output Output_2,
  output Output_3,
  output Output_4,
  output Output_5,
  output Output_6,
  output Output_7
);

  wire not_1_out, not_2_out, not_3_out;

  not not_1 (not_1_out, A2);
  not not_2 (not_2_out, A1);
  not not_3 (not_3_out, A0);
  and AND (Output_0, not_2_out, not_3_out, not_1_out);
  and AND_2 (Output_1, A0, not_2_out, not_1_out);
  and AND_3 (Output_2, not_3_out, A1, not_1_out);
  and AND_4 (Output_3, A0, A1, not_1_out);
  and AND_5 (Output_4, not_3_out, not_2_out, A2);
  and AND_6 (Output_5, A0, not_2_out, A2);
  and AND_7 (Output_6, not_3_out, A1, A2);
  and AND_8 (Output_7, A0, A1, A2);
endmodule
