// Logisim project MUX.circ as structural Verilog: 6 circuits, main circuit 4:1MUX
module _4_1MUX (
  input  S0,
  input  S1,
  input  D0,
  input  D1,
  input  D2,
  input  D3,
  output Y
);

  wire AND_2_out, AND_3_out, AND_4_out, AND_out, NOT_2_out, NOT_out;

  not NOT (NOT_out, S0);
  not NOT_2 (NOT_2_out, S1);
  and AND (AND_out, NOT_out, D0, NOT_2_out);
  and AND_2 (AND_2_out, NOT_out, D1, S1);
  and AND_3 (AND_3_out, S0, D2, NOT_2_out);
  and AND_4 (AND_4_out, S0, D3, S1);
  or OR (Y, AND_out, AND_2_out, AND_3_out, AND_4_out);

  // Notes on the sheet:
  //   4:1Multiplexer_PRIYANSHU_2100321540124
endmodule

module _2_1MUX (
  input  S0,
  input  D0,
  input  D1,
  output Y
);

  wire AND_2_out, AND_out, NOT_out;

  not NOT (NOT_out, S0);
  and AND (AND_out, D0, NOT_out);
  and AND_2 (AND_2_out, D1, S0);
  or OR (Y, AND_out, AND_2_out);

  // Notes on the sheet:
  //   2:1Multiplexer_PRIYANSHU_2100321540124
endmodule

module _8_1MUX (
  input  D0,
  input  D1,
  input  D2,
  input  D3,
  input  D4,
  input  D5,
  input  D6,
  input  D7,
  input  in_9,
  input  [2:0] in_10,
  output Y
);

  Multiplexer #(.select(3)) multiplexer_1 (
    .in0(D0), .in1(D1), .in2(D2), .in3(D3), .in4(D4), .in5(D5), .in6(D6), .in7(D7), .out(Y), .sel(in_10),
    .en(in_9));

  // Notes on the sheet:
  //   8:1Multiplexer_PRIYANSHU_2100321540124
endmodule

module _8_1MUXusing2_1 (
  input  D0,
  input  D1,
  input  D2,
  input  D3,
  input  in_5,
  input  in_6,
  input  D4,
  input  D5,
  input  in_9,
  input  D6,
  input  D7,
  output Y
);

  wire multiplexer_1_out, multiplexer_2_out, multiplexer_3_out, multiplexer_4_out, multiplexer_5_out,
       multiplexer_7_out;

  Multiplexer #(.enable("false")) multiplexer_1 (.in0(D0), .in1(D1), .out(multiplexer_1_out), .sel(in_5));
  Multiplexer #(.enable("false")) multiplexer_2 (.in0(D2), .in1(D3), .out(multiplexer_2_out), .sel(in_5));
  Multiplexer #(.enable("false")) multiplexer_3 (.in0(D4), .in1(D5), .out(multiplexer_3_out), .sel(in_5));
  Multiplexer #(.enable("false")) multiplexer_4 (.in0(D6), .in1(D7), .out(multiplexer_4_out), .sel(in_5));
  Multiplexer #(.enable("false")) multiplexer_5 (
    .in0(multiplexer_1_out), .in1(multiplexer_2_out), .out(multiplexer_5_out), .sel(in_6));
  Multiplexer #(.enable("false")) multiplexer_6 (.in0(multiplexer_5_out), .in1(multiplexer_7_out), .out(Y), .sel(in_9));
  Multiplexer #(.enable("false")) multiplexer_7 (
    .in0(multiplexer_3_out), .in1(multiplexer_4_out), .out(multiplexer_7_out), .sel(in_6));

  // Notes on the sheet:
  //   8:1Multiplexerusing2:1_PRIYANSHU_2100321540124
endmodule

module _8_1MUXusing4_1 (
  input  D0,
  input  D1,
  input  D2,
  input  D3,
  input  [1:0] D4,
  input  in_6,
  input  D5,
  input  in_8,
  input  D6,
  input  D7,
  output Y
);

  wire multiplexer_1_out, multiplexer_3_out;

  Multiplexer #(.select(2), .enable("false")) multiplexer_1 (
    .in0(D0), .in1(D1), .in2(D2), .in3(D3), .out(multiplexer_1_out), .sel(D4));
  Multiplexer #(.enable("false")) multiplexer_2 (.in0(multiplexer_1_out), .in1(multiplexer_3_out), .out(Y), .sel(in_8));
  Multiplexer #(.select(2), .enable("false")) multiplexer_3 (
    .in0(in_6), .in1(D5), .in2(D6), .in3(D7), .out(multiplexer_3_out), .sel(D4));

  // Notes on the sheet:
  //   8:1Multiplexerusing4:1_PRIYANSHU_2100321540124
endmodule

module _16_1Multiusing4_1 (
  input  D0,
  input  D1,
  input  D2,
  input  D3,
  input  D4,
  input  D5,
  input  D6,
  input  D7,
  input  [1:0] in_9,
  input  D8,
  input  D9,
  input  D10,
  input  [1:0] in_13,
  input  D11,
  input  D12,
  input  D13,
  input  D14,
  input  D15,
  output Y
);

  wire multiplexer_1_out, multiplexer_2_out, multiplexer_3_out, multiplexer_4_out;

  Multiplexer #(.select(2), .enable("false")) multiplexer_1 (
    .in0(D0), .in1(D1), .in2(D2), .in3(D3), .out(multiplexer_1_out), .sel(in_9));
  Multiplexer #(.select(2), .enable("false")) multiplexer_2 (
    .in0(D4), .in1(D5), .in2(D6), .in3(D7), .out(multiplexer_2_out), .sel(in_9));
  Multiplexer #(.select(2), .enable("false")) multiplexer_3 (
    .in0(D8), .in1(D9), .in2(D10), .in3(D11), .out(multiplexer_3_out), .sel(in_9));
  Multiplexer #(.select(2), .enable("false")) multiplexer_4 (
    .in0(D12), .in1(D13), .in2(D14), .in3(D15), .out(multiplexer_4_out), .sel(in_9));
  Multiplexer #(.select(2), .enable("false")) multiplexer_5 (
    .in0(multiplexer_1_out), .in1(multiplexer_2_out), .in2(multiplexer_3_out), .in3(multiplexer_4_out),
    .out(Y), .sel(in_13));

  // Notes on the sheet:
  //   16:1Multiplexerusing4:1_PRIYANSHU_2100321540124
endmodule
