// Logisim project Experiment_7.circ as structural Verilog: 6 circuits, main circuit SR Latch NAND
module SR_Latch_NAND (
  input  S,
  input  R,
  output Q,
  output Q_prime
);

  nand NAND (Q, S, Q_prime);
  nand NAND_2 (Q_prime, Q, R);

  // Notes on the sheet:
  //   SR Latch NAND_PRIYANSHU_2100321540124
endmodule

module SR_Latch_NOR (
  input  R,
  input  S,
  output Q,
  output Q_prime
);

  nor NOR (Q, R, Q_prime);
  nor NOR_2 (Q_prime, Q, S);

  // Notes on the sheet:
  //   SR Latch NOR_PRIYANSHU_2100321540124
endmodule

module SR_Flipflop (
  input  R,
  input  S,
  output Q,
  output Q_prime
);

  wire AND_2_out, AND_out, clock_1_out;

  Clock clock_1 (.out(clock_1_out));
  and AND (AND_out, R, clock_1_out);
  and AND_2 (AND_2_out, clock_1_out, S);
  nor NOR (Q, AND_out, Q_prime);
  nor NOR_2 (Q_prime, Q, AND_2_out);

  // Notes on the sheet:
  //   Clock
  //   SR Flip-Flop_PRIYANSHU_2100321540124
endmodule

module D_Flipflop (
  input  D,
  output Q,
  output Q_prime
);

  wire AND_2_out, AND_out, clock_1_out, not_1_out;

  not not_1 (not_1_out, D);
  Clock clock_1 (.out(clock_1_out));
  and AND (AND_out, not_1_out, clock_1_out);
  and AND_2 (AND_2_out, clock_1_out, D);
  nor NOR (Q, AND_out, Q_prime);
  nor NOR_2 (Q_prime, Q, AND_2_out);

  // Notes on the sheet:
  //   Clock
  //   D Flip-Flop_PRIYANSHU_2100321540124
endmodule

module SR_Flipflop_Logisim (
  input  R,
  input  S,
  output Q,
  output Q_prime
);

  wire clock_1_out;

  Clock clock_1 (.out(clock_1_out));
  S_R_Flip_Flop s_r_ff_1 (.S(R), .clk(clock_1_out), .R(S), .Q(Q), .Qn(Q_prime));  // open: preset, reset, en

  // Notes on the sheet:
  //   Clock
  //   SR Flip-Flop_PRIYANSHU_2100321540124
endmodule

module D_Flipflop_Logisim (
  input  in_1,
  input  in_2,
  input  in_3,
  input  in_4,
  output out_5,
  output out_6
);

  wire clock_1_out;

  Clock clock_1 (.out(clock_1_out));
  D_Flip_Flop d_ff_1 (.clk(clock_1_out), .D(in_1), .Q(out_5), .Qn(out_6), .preset(in_2), .en(in_3), .reset(in_4));

  // Notes on the sheet:
  //   D Flip-Flop_PRIYANSHU_2100321540124
endmodule
