// Logisim project Experiment_8.circ as structural Verilog: 2 circuits, main circuit T Flip-Flop
module T_Flip_Flop (
  input  T,
  output Q,
  output Q_prime
);

  wire AND_2_out, AND_out, Clock_out;

  Clock Clock (.out(Clock_out));
  and AND (AND_out, Q, T, Clock_out);
  and AND_2 (AND_2_out, Clock_out, T, Q_prime);
  nor NOR (Q, AND_out, Q_prime);
  nor NOR_2 (Q_prime, Q, AND_2_out);

  // Notes on the sheet:
  //   T Flip-Flop_PRIYANSHU_2100321540124
endmodule

module JK_Flip_Flop (
  input  K,
  input  J,
  output Q,
  output Q_prime
);

  wire AND_2_out, AND_out, Clock_out;

  Clock Clock (.out(Clock_out));
  and AND (AND_out, Q, K, Clock_out);
  and AND_2 (AND_2_out, Clock_out, J, Q_prime);
  nor NOR (Q, AND_out, Q_prime);
  nor NOR_2 (Q_prime, Q, AND_2_out);

  // Notes on the sheet:
  //   JK Flip-Flop_PRIYANSHU_2100321540124
endmodule
