// Logisim project Experiment_9.circ as structural Verilog: 1 circuit, main circuit 4 bit Universal Shift Register
module _4_bit_Universal_Shift_Register (
  input  Shift_Right,
  input  _14,
  input  _13,
  input  _12,
  input  Shift_Left,
  input  _11,
  input  [1:0] Selection_Bits,
  output A4,
  output A3,
  output A2,
  output A1
);

  wire Clock_out, CLR_out, multiplexer_1_out, multiplexer_2_out, multiplexer_3_out, multiplexer_4_out;

  Multiplexer #(.select(2), .enable("false")) multiplexer_1 (
    .in0(A4), .in1(Shift_Right), .in2(A3), .in3(_14), .out(multiplexer_1_out), .sel(Selection_Bits));
  Multiplexer #(.select(2), .enable("false")) multiplexer_2 (
    .in0(A3), .in1(A4), .in2(A2), .in3(_13), .out(multiplexer_2_out), .sel(Selection_Bits));
  Multiplexer #(.select(2), .enable("false")) multiplexer_3 (
    .in0(A2), .in1(A3), .in2(A1), .in3(_12), .out(multiplexer_3_out), .sel(Selection_Bits));
  Multiplexer #(.select(2), .enable("false")) multiplexer_4 (
    .in0(A1), .in1(A2), .in2(Shift_Left), .in3(_11), .out(multiplexer_4_out), .sel(Selection_Bits));
  Clock Clock (.out(Clock_out));
  D_Flip_Flop d_ff_1 (.clk(Clock_out), .D(multiplexer_1_out), .Q(A4), .reset(CLR_out));  // open: Qn, preset, en
  D_Flip_Flop d_ff_2 (.clk(Clock_out), .D(multiplexer_2_out), .Q(A3), .reset(CLR_out));  // open: Qn, preset, en
  D_Flip_Flop d_ff_3 (.clk(Clock_out), .D(multiplexer_3_out), .Q(A2), .reset(CLR_out));  // open: Qn, preset, en
  D_Flip_Flop d_ff_4 (.clk(Clock_out), .D(multiplexer_4_out), .Q(A1), .reset(CLR_out));  // open: Qn, preset, en
  Button CLR (.out(CLR_out));

  // Notes on the sheet:
  //   4 bit Universal Shift Register_PRIYANSHU_2100321540124
endmodule
